# Fritzing sketch ESP8266 Hookup (saved by Fritzing 1.0.1rc)

parts:
  Part1 = RFID-RC522-v3
  Mod1 = Amica NodeMCU DEVKIT 1.0

nets:
  N1: Part1.SDA, Mod1.pin_13
  N2: Part1.SCK, Mod1.pin8
  N3: Part1.MOSI, Mod1.pin6
  N4: Part1.MISO, Mod1.pin7
  N5: Part1.GND, Mod1.pin2, Mod1.pin_9
  N6: Part1.RST, Mod1.pin_14
  N7: Part1.3.3V, Mod1.pin1, Mod1.pin_10

custom parts:
  RFID-RC522-v3: A simple China made RFID-RC522 Reader (6x4 cm); do check the pin labels, as this is a MFRC522 based clone.
